# Fritzing sketch Blink_LED (saved by Fritzing 0.9.2b)
breadboards: 1

parts:
  Raspberry_Pi3 = Raspberry Pi 2
  LED1 = LED - 5mm [color="Red (633nm)" package="5 mm [THT]"]
  R1 = Resistor [tolerance=±5% resistance=560 package=THT]

nets:
  N1: Raspberry_Pi3.GPIO5, LED1.cathode
  N2: Raspberry_Pi3.5V, R1.Pin_0
  N3: LED1.anode, R1.Pin_1
